# Fritzing sketch organduino00 (saved by Fritzing 0.9.2b)
circuit board: 11.4148cm x 9.10362cm
breadboards: 1

parts:
  J1 = female pin header, 12 pins [form="♀ (female)"]
  J2 = female pin header, 12 pins [form="♀ (female)"]
  J3 = female pin header, 12 pins [form="♀ (female)"]
  J4 = female pin header, 12 pins [form="♀ (female)"]  # not connected
  J5 = female pin header, 12 pins [form="♀ (female)"]  # not connected
  J6 = female pin header, 13 pins [form="♀ (female)"]
  D11 = DIODE-SCHOTTKY [package=sma-diode]
  D12 = DIODE-SCHOTTKY [package=sma-diode]
  D13 = DIODE-SCHOTTKY [package=sma-diode]
  D14 = DIODE-SCHOTTKY [package=sma-diode]
  D15 = DIODE-SCHOTTKY [package=sma-diode]
  D16 = DIODE-SCHOTTKY [package=sma-diode]
  D17 = DIODE-SCHOTTKY [package=sma-diode]
  D18 = DIODE-SCHOTTKY [package=sma-diode]
  D19 = DIODE-SCHOTTKY [package=sma-diode]
  D20 = DIODE-SCHOTTKY [package=sma-diode]
  D21 = DIODE-SCHOTTKY [package=sma-diode]
  D22 = DIODE-SCHOTTKY [package=sma-diode]
  D23 = DIODE-SCHOTTKY [package=sma-diode]
  D24 = DIODE-SCHOTTKY [package=sma-diode]
  D25 = DIODE-SCHOTTKY [package=sma-diode]  # not connected
  D26 = DIODE-SCHOTTKY [package=sma-diode]  # not connected
  D27 = DIODE-SCHOTTKY [package=sma-diode]  # not connected
  D29 = DIODE-SCHOTTKY [package=sma-diode]  # not connected
  D30 = DIODE-SCHOTTKY [package=sma-diode]  # not connected
  D31 = DIODE-SCHOTTKY [package=sma-diode]  # not connected
  D32 = DIODE-SCHOTTKY [package=sma-diode]  # not connected
  D33 = DIODE-SCHOTTKY [package=sma-diode]  # not connected
  D34 = DIODE-SCHOTTKY [package=sma-diode]  # not connected
  D35 = DIODE-SCHOTTKY [package=sma-diode]  # not connected
  D36 = DIODE-SCHOTTKY [package=sma-diode]  # not connected
  D37 = DIODE-SCHOTTKY [package=sma-diode]  # not connected
  D38 = DIODE-SCHOTTKY [package=sma-diode]  # not connected
  D39 = DIODE-SCHOTTKY [package=sma-diode]  # not connected
  D40 = DIODE-SCHOTTKY [package=sma-diode]  # not connected
  D41 = DIODE-SCHOTTKY [package=sma-diode]  # not connected
  D42 = DIODE-SCHOTTKY [package=sma-diode]  # not connected
  D43 = DIODE-SCHOTTKY [package=sma-diode]  # not connected
  D44 = DIODE-SCHOTTKY [package=sma-diode]  # not connected
  D45 = DIODE-SCHOTTKY [package=sma-diode]  # not connected
  D46 = DIODE-SCHOTTKY [package=sma-diode]  # not connected
  D47 = DIODE-SCHOTTKY [package=sma-diode]  # not connected
  D48 = DIODE-SCHOTTKY [package=sma-diode]  # not connected
  D49 = DIODE-SCHOTTKY [package=sma-diode]  # not connected
  D50 = DIODE-SCHOTTKY [package=sma-diode]
  D51 = DIODE-SCHOTTKY [package=sma-diode]
  D52 = DIODE-SCHOTTKY [package=sma-diode]
  D53 = DIODE-SCHOTTKY [package=sma-diode]
  D54 = DIODE-SCHOTTKY [package=sma-diode]
  D55 = DIODE-SCHOTTKY [package=sma-diode]
  D56 = DIODE-SCHOTTKY [package=sma-diode]
  D57 = DIODE-SCHOTTKY [package=sma-diode]
  D58 = DIODE-SCHOTTKY [package=sma-diode]
  D59 = DIODE-SCHOTTKY [package=sma-diode]
  D60 = DIODE-SCHOTTKY [package=sma-diode]
  D62 = DIODE-SCHOTTKY [package=sma-diode]
  D63 = DIODE-SCHOTTKY [package=sma-diode]
  D64 = DIODE-SCHOTTKY [package=sma-diode]
  D65 = DIODE-SCHOTTKY [package=sma-diode]
  D66 = DIODE-SCHOTTKY [package=sma-diode]
  D67 = DIODE-SCHOTTKY [package=sma-diode]
  D68 = DIODE-SCHOTTKY [package=sma-diode]
  D69 = DIODE-SCHOTTKY [package=sma-diode]
  D70 = DIODE-SCHOTTKY [package=sma-diode]
  D71 = DIODE-SCHOTTKY [package=sma-diode]
  D72 = DIODE-SCHOTTKY [package=sma-diode]
  D73 = DIODE-SCHOTTKY [package=sma-diode]
  D81 = DIODE-SCHOTTKY [package=sma-diode]
  D82 = DIODE-SCHOTTKY [package=sma-diode]
  D83 = DIODE-SCHOTTKY [package=sma-diode]
  D84 = DIODE-SCHOTTKY [package=sma-diode]
  D85 = DIODE-SCHOTTKY [package=sma-diode]
  D86 = DIODE-SCHOTTKY [package=sma-diode]
  D87 = DIODE-SCHOTTKY [package=sma-diode]
  D88 = DIODE-SCHOTTKY [package=sma-diode]
  SJ1 = Solder Jumper [package=sj_2s-notrace]
  Part1 = Arduino Mega 2560 (Rev3)
  SJ2 = Solder Jumper [package=sj_2s-notrace]
  SJ3 = Solder Jumper [package=sj_2s-notrace]
  SJ4 = Solder Jumper [package=sj_2s-notrace]
  SJ5 = Solder Jumper [package=sj_2s-notrace]
  SJ7 = Solder Jumper [package=sj_2s-notrace]
  SJ8 = Solder Jumper [package=sj_2s-notrace]
  D9 = DIODE-SCHOTTKY [package=sma-diode]
  D10 = DIODE-SCHOTTKY [package=sma-diode]
  J7 = female pin header, 12 pins [form="♀ (female)"]
  J8 = female pin header, 3 pins [form="♀ (female)"]

nets:
  N1: J1.pin1, D62.C
  N2: J1.pin2, D72.C
  N3: J1.pin3, D66.C
  N4: J1.pin4, D65.C
  N5: J1.pin5, D63.C
  N6: J1.pin6, D70.C
  N7: J1.pin7, D64.C
  N8: J1.pin8, D68.C
  N9: J1.pin9, D73.C
  N10: J1.pin10, D71.C
  N11: J1.pin11, D67.C
  N12: J1.pin12, D69.C
  N13: J2.pin1, D87.C
  N14: J2.pin2, D85.C
  N15: J2.pin3, D86.C
  N16: J2.pin4, D83.C
  N17: J2.pin5, D84.C
  N18: J2.pin6, D82.C
  N19: J2.pin7, D81.C
  N20: J2.pin9, D9.C
  N21: J2.pin10, D10.C
  N22: J2.pin11, D11.C
  N23: J2.pin12, D12.C
  N24: J3.pin1, D50.C
  N25: J3.pin2, D51.C
  N26: J3.pin3, D52.C
  N27: J3.pin4, D53.C
  N28: J3.pin5, D56.C
  N29: J3.pin6, D54.C
  N30: J3.pin7, D55.C
  N31: J3.pin8, D57.C
  N32: J3.pin9, D60.C
  N33: J3.pin10, D58.C
  N34: J3.pin11, D59.C
  N35: J3.pin12, D88.C
  N36: J6.pin1, Part1.A0
  N37: J6.pin2, D24.C
  N38: J6.pin3, D23.C
  N39: J6.pin4, D22.C
  N40: J6.pin5, D21.C
  N41: J6.pin6, D20.C
  N42: J6.pin7, D19.C
  N43: J6.pin8, D18.C
  N44: J6.pin9, D17.C
  N45: J6.pin10, D16.C
  N46: J6.pin11, D15.C
  N47: J6.pin12, D14.C
  N48: J6.pin13, D13.C
  N49: D11.A, Part1.D26
  N50: D12.A, Part1.D28
  N51: D13.A, Part1.D30
  N52: D14.A, Part1.D32
  N53: D15.A, Part1.D34
  N54: D16.A, Part1.D36
  N55: D17.A, Part1.D38
  N56: D18.A, Part1.D40
  N57: D19.A, Part1.D42
  N58: D20.A, Part1.D44
  N59: D21.A, Part1.D46
  N60: D22.A, Part1.D48
  N61: D23.A, Part1.D50
  N62: D24.A, Part1.D52
  N63: D50.A, Part1.A12
  N64: D51.A, Part1.A11
  N65: D52.A, Part1.A10
  N66: D53.A, Part1.A9
  N67: D54.A, Part1.A7
  N68: D55.A, Part1.A6
  N69: D56.A, Part1.A8
  N70: D57.A, Part1.A5
  N71: D58.A, Part1.A3
  N72: D59.A, Part1.A2
  N73: D60.A, Part1.A4
  N74: D81.A, Part1.D13_PWM
  N75: D82.A, Part1.D12_PWM
  N76: D83.A, Part1.D10_PWM
  N77: D84.A, Part1.D11_PWM
  N78: D85.A, Part1.D8_PWM
  N79: D86.A, Part1.D9_PWM
  N80: D87.A, Part1.D7_PWM
  N81: D88.A, Part1.A1
  N82: SJ1.1, Part1.D6_PWM
  N83: SJ1.2, SJ2.2, SJ3.2, SJ4.2, SJ5.2, SJ7.2, SJ8.2, J7.pin1, J7.pin2, J7.pin3, J7.pin4, J7.pin5, J7.pin6, J7.pin7, J7.pin8, J7.pin9, J7.pin10, J7.pin11, J7.pin12
  N84: Part1.A13, J8.pin3
  N85: Part1.A14, J8.pin2
  N86: Part1.A15, J8.pin1
  N87: Part1.D0_RX0, SJ7.1
  N88: Part1.D1_TX0, SJ5.1
  N89: Part1.D2_PWM, SJ8.1
  N90: Part1.D3_PWM, SJ4.1
  N91: Part1.D4_PWM, SJ3.1
  N92: Part1.D5_PWM, SJ2.1
  N93: Part1.D22, D9.A
  N94: Part1.D24, D10.A
