# Fritzing sketch organduino7 (saved by Fritzing 0.9.2b)
circuit board: 10.7938cm x 8.21765cm

parts:
  Octave0 = female pin header, 12 pins [form="♀ (female)"]
  Octave1 = female pin header, 12 pins [form="♀ (female)"]
  Octave2 = female pin header, 12 pins [form="♀ (female)"]
  Octave3 = female pin header, 12 pins [form="♀ (female)"]
  Octave4+1 = female pin header, 13 pins [form="♀ (female)"]
  D0 = DIODE-SCHOTTKY [package=sma-diode]
  D1 = DIODE-SCHOTTKY [package=sma-diode]
  D2 = DIODE-SCHOTTKY [package=sma-diode]
  D3 = DIODE-SCHOTTKY [package=sma-diode]
  Part1 = Arduino Mega 2560 (Rev3)
  Rank0 = Solder Jumper [package=sj_2s-no]
  Rank1 = Solder Jumper [package=sj_2s-no]
  Rank3 = Solder Jumper [package=sj_2s-no]
  Rank2 = Solder Jumper [package=sj_2s-no]
  Pedal0-3 = female pin header, 4 pins [form="♀ (female)"]
  D24 = DIODE-SCHOTTKY [package=sma-diode]
  D25 = DIODE-SCHOTTKY [package=sma-diode]
  D26 = DIODE-SCHOTTKY [package=sma-diode]
  D27 = DIODE-SCHOTTKY [package=sma-diode]
  D28 = DIODE-SCHOTTKY [package=sma-diode]
  D29 = DIODE-SCHOTTKY [package=sma-diode]
  D30 = DIODE-SCHOTTKY [package=sma-diode]
  D31 = DIODE-SCHOTTKY [package=sma-diode]
  D32 = DIODE-SCHOTTKY [package=sma-diode]
  D33 = DIODE-SCHOTTKY [package=sma-diode]
  D34 = DIODE-SCHOTTKY [package=sma-diode]
  D35 = DIODE-SCHOTTKY [package=sma-diode]
  Pedal3_or_Rank5 = Solder Jumper [package=sj_2]
  Rank4 = Solder Jumper [package=sj_2s-no]
  D37 = DIODE-SCHOTTKY [package=sma-diode]
  D38 = DIODE-SCHOTTKY [package=sma-diode]
  D39 = DIODE-SCHOTTKY [package=sma-diode]
  D40 = DIODE-SCHOTTKY [package=sma-diode]
  D41 = DIODE-SCHOTTKY [package=sma-diode]
  D42 = DIODE-SCHOTTKY [package=sma-diode]
  D43 = DIODE-SCHOTTKY [package=sma-diode]
  D44 = DIODE-SCHOTTKY [package=sma-diode]
  D45 = DIODE-SCHOTTKY [package=sma-diode]
  D46 = DIODE-SCHOTTKY [package=sma-diode]
  D36 = DIODE-SCHOTTKY [package=sma-diode]
  D47 = DIODE-SCHOTTKY [package=sma-diode]
  D60 = DIODE-SCHOTTKY [package=sma-diode]
  D59 = DIODE-SCHOTTKY [package=sma-diode]
  D58 = DIODE-SCHOTTKY [package=sma-diode]
  D57 = DIODE-SCHOTTKY [package=sma-diode]
  D56 = DIODE-SCHOTTKY [package=sma-diode]
  D55 = DIODE-SCHOTTKY [package=sma-diode]
  D54 = DIODE-SCHOTTKY [package=sma-diode]
  D53 = DIODE-SCHOTTKY [package=sma-diode]
  D52 = DIODE-SCHOTTKY [package=sma-diode]
  D51 = DIODE-SCHOTTKY [package=sma-diode]
  D50 = DIODE-SCHOTTKY [package=sma-diode]
  D49 = DIODE-SCHOTTKY [package=sma-diode]
  D48 = DIODE-SCHOTTKY [package=sma-diode]
  J1 = double row female pin header, 12 pins [form="♀ (female)"]
  Drive_pins = double row female pin header, 12 pins [form="♀ (female)"]
  D4 = DIODE-SCHOTTKY [package=sma-diode]
  D5 = DIODE-SCHOTTKY [package=sma-diode]
  D6 = DIODE-SCHOTTKY [package=sma-diode]
  D7 = DIODE-SCHOTTKY [package=sma-diode]
  D9 = DIODE-SCHOTTKY [package=sma-diode]
  D8 = DIODE-SCHOTTKY [package=sma-diode]
  D12 = DIODE-SCHOTTKY [package=sma-diode]
  D13 = DIODE-SCHOTTKY [package=sma-diode]
  D17 = DIODE-SCHOTTKY [package=sma-diode]
  D16 = DIODE-SCHOTTKY [package=sma-diode]
  D15 = DIODE-SCHOTTKY [package=sma-diode]
  D14 = DIODE-SCHOTTKY [package=sma-diode]
  D23 = DIODE-SCHOTTKY [package=sma-diode]
  D19 = DIODE-SCHOTTKY [package=sma-diode]
  D20 = DIODE-SCHOTTKY [package=sma-diode]
  D18 = DIODE-SCHOTTKY [package=sma-diode]
  D22 = DIODE-SCHOTTKY [package=sma-diode]
  D21 = DIODE-SCHOTTKY [package=sma-diode]
  D10 = DIODE-SCHOTTKY [package=sma-diode]
  D11 = DIODE-SCHOTTKY [package=sma-diode]

nets:
  N1: Octave0.pin1, D11.C
  N2: Octave0.pin2, D10.C
  N3: Octave0.pin3, D9.C
  N4: Octave0.pin4, D8.C
  N5: Octave0.pin5, D7.C
  N6: Octave0.pin6, D6.C
  N7: Octave0.pin7, D5.C
  N8: Octave0.pin8, D4.C
  N9: Octave0.pin9, D3.C
  N10: Octave0.pin10, D2.C
  N11: Octave0.pin11, D1.C
  N12: Octave0.pin12, D0.C
  N13: Octave1.pin1, D23.C
  N14: Octave1.pin2, D22.C
  N15: Octave1.pin3, D21.C
  N16: Octave1.pin4, D20.C
  N17: Octave1.pin5, D19.C
  N18: Octave1.pin6, D18.C
  N19: Octave1.pin7, D17.C
  N20: Octave1.pin8, D16.C
  N21: Octave1.pin9, D15.C
  N22: Octave1.pin10, D14.C
  N23: Octave1.pin11, D13.C
  N24: Octave1.pin12, D12.C
  N25: Octave2.pin1, D35.C
  N26: Octave2.pin2, D34.C
  N27: Octave2.pin3, D33.C
  N28: Octave2.pin4, D32.C
  N29: Octave2.pin5, D31.C
  N30: Octave2.pin6, D30.C
  N31: Octave2.pin7, D29.C
  N32: Octave2.pin8, D28.C
  N33: Octave2.pin9, D27.C
  N34: Octave2.pin10, D26.C
  N35: Octave2.pin11, D25.C
  N36: Octave2.pin12, D24.C
  N37: Octave3.pin1, D47.C
  N38: Octave3.pin2, D46.C
  N39: Octave3.pin3, D45.C
  N40: Octave3.pin4, D44.C
  N41: Octave3.pin5, D43.C
  N42: Octave3.pin6, D42.C
  N43: Octave3.pin7, D41.C
  N44: Octave3.pin8, D40.C
  N45: Octave3.pin9, D39.C
  N46: Octave3.pin10, D38.C
  N47: Octave3.pin11, D37.C
  N48: Octave3.pin12, D36.C
  N49: Octave4+1.pin1, D60.C
  N50: Octave4+1.pin2, D59.C
  N51: Octave4+1.pin3, D58.C
  N52: Octave4+1.pin4, D57.C
  N53: Octave4+1.pin5, D56.C
  N54: Octave4+1.pin6, D55.C
  N55: Octave4+1.pin7, D54.C
  N56: Octave4+1.pin8, D53.C
  N57: Octave4+1.pin9, D52.C
  N58: Octave4+1.pin10, D51.C
  N59: Octave4+1.pin11, D50.C
  N60: Octave4+1.pin12, D49.C
  N61: Octave4+1.pin13, D48.C
  N62: D0.A, Part1.D28
  N63: D1.A, Part1.D26
  N64: D2.A, Part1.D24
  N65: D3.A, Part1.D22
  N66: Part1.A8, D40.A
  N67: Part1.A9, D39.A
  N68: Part1.A10, D38.A
  N69: Part1.A11, D37.A
  N70: Part1.A12, Pedal0-3.pin1
  N71: Part1.A13, Pedal0-3.pin2
  N72: Part1.A14, Pedal0-3.pin3
  N73: Part1.A15, Pedal3_or_Rank5.2
  N74: Part1.A0, D48.A
  N75: Part1.A1, D47.A
  N76: Part1.A2, D46.A
  N77: Part1.A3, D45.A
  N78: Part1.A4, D44.A
  N79: Part1.A5, D43.A
  N80: Part1.A6, D42.A
  N81: Part1.A7, D41.A
  N82: Part1.D21/SCL, Part1.SCL, D20.A
  N83: Part1.D20/SDA, Part1.SDA, D19.A
  N84: Part1.D19/RX1, D18.A
  N85: Part1.D18/TX1, D17.A
  N86: Part1.D17_PWM/RX2, D16.A
  N87: Part1.D16_PWM/TX2, D15.A
  N88: Part1.D15/RX3, D14.A
  N89: Part1.D14/TX3, D13.A
  N90: Part1.D13_PWM, D4.A
  N91: Part1.D12_PWM, D5.A
  N92: Part1.D11_PWM, D6.A
  N93: Part1.D10_PWM, D7.A
  N94: Part1.D9_PWM, D8.A
  N95: Part1.D8_PWM, D9.A
  N96: Part1.D0_RX0, D12.A
  N97: Part1.D1_TX0, Rank4.1
  N98: Part1.D2_PWM, Rank3.1
  N99: Part1.D3_PWM, Rank2.1
  N100: Part1.D4_PWM, Rank1.1
  N101: Part1.D5_PWM, Rank0.1
  N102: Part1.D6_PWM, D11.A
  N103: Part1.D7_PWM, D10.A
  N104: Part1.D23, D23.A
  N105: Part1.D25, D22.A
  N106: Part1.D27, D21.A
  N107: Part1.D29, D24.A
  N108: Part1.D30, D60.A
  N109: Part1.D31, D25.A
  N110: Part1.D32, D59.A
  N111: Part1.D33, D26.A
  N112: Part1.D34, D58.A
  N113: Part1.D35, D27.A
  N114: Part1.D36, D57.A
  N115: Part1.D37, D28.A
  N116: Part1.D38, D56.A
  N117: Part1.D39, D29.A
  N118: Part1.D40, D55.A
  N119: Part1.D41, D30.A
  N120: Part1.D42, D54.A
  N121: Part1.D43, D31.A
  N122: Part1.D44, D53.A
  N123: Part1.D45, D32.A
  N124: Part1.D46, D52.A
  N125: Part1.D47, D33.A
  N126: Part1.D48, D51.A
  N127: Part1.D49, D34.A
  N128: Part1.D50, D50.A
  N129: Part1.D51, D35.A
  N130: Part1.D52, D49.A
  N131: Part1.D53, D36.A
  N132: Rank0.2, Rank1.2, Rank3.2, Rank2.2, Pedal3_or_Rank5.3, Rank4.2, J1.pin1, J1.pin2, J1.pin3, J1.pin4, J1.pin5, J1.pin6, J1.pin7, J1.pin8, J1.pin9, J1.pin10, J1.pin11, J1.pin12, Drive_pins.pin1, Drive_pins.pin2, Drive_pins.pin3, Drive_pins.pin4, Drive_pins.pin5, Drive_pins.pin6, Drive_pins.pin7, Drive_pins.pin8, Drive_pins.pin9, Drive_pins.pin10, Drive_pins.pin11, Drive_pins.pin12
  N133: Pedal0-3.pin4, Pedal3_or_Rank5.1

notes:
  OrganDuino
  v1.0
  Right pad
  jumper controlled
  Drive pin(s)
